// Logisim project halfAdder.circ as structural Verilog
module half_Adder (
  input  a,
  input  b,
  output Carry,
  output Out
);

  and and_1 (Carry, a, b);
  xor xor_1 (Out, a, b);
endmodule

module Full_Adder (
  input  Carry_in,
  input  in_2,
  input  b_in,
  output out_4,
  output Carry
);

  wire half_adder_1_carry, half_adder_1_out, half_adder_2_carry;

  half_Adder half_adder_1 (.a(in_2), .b(b_in), .Carry(half_adder_1_carry), .Out(half_adder_1_out));
  half_Adder half_adder_2 (.a(Carry_in), .b(half_adder_1_out), .Carry(half_adder_2_carry), .Out(out_4));
  or or_1 (Carry, half_adder_2_carry, half_adder_1_carry);

  // Notes on the sheet:
  //   a in
  //   Result
endmodule

module Adder_8_bits (
  input  a0,
  input  a1,
  input  a2,
  input  a3,
  input  a4,
  input  a5,
  input  a6,
  input  a7,
  input  b0,
  input  b1,
  input  b2,
  input  b3,
  input  b4,
  input  b5,
  input  b6,
  input  b7,
  output r0,
  output r1,
  output r2,
  output r3,
  output r4,
  output r5,
  output r6,
  output r7,
  output Overflow
);

  wire button_1_out, full_adder_1_carry, full_adder_2_carry, full_adder_3_carry, full_adder_4_carry,
       full_adder_5_carry, full_adder_6_carry, full_adder_7_carry;

  Button button_1 (.out(button_1_out));
  Full_Adder full_adder_1 (.Carry_in(button_1_out), .in_2(a0), .b_in(b0), .out_4(r0), .Carry(full_adder_1_carry));
  Full_Adder full_adder_2 (.Carry_in(full_adder_1_carry), .in_2(a1), .b_in(b1), .out_4(r1), .Carry(full_adder_2_carry));
  Full_Adder full_adder_3 (.Carry_in(full_adder_2_carry), .in_2(a2), .b_in(b2), .out_4(r2), .Carry(full_adder_3_carry));
  Full_Adder full_adder_4 (.Carry_in(full_adder_3_carry), .in_2(a3), .b_in(b3), .out_4(r3), .Carry(full_adder_4_carry));
  Full_Adder full_adder_5 (.Carry_in(full_adder_4_carry), .in_2(a4), .b_in(b4), .out_4(r4), .Carry(full_adder_5_carry));
  Full_Adder full_adder_6 (.Carry_in(full_adder_5_carry), .in_2(a5), .b_in(b5), .out_4(r5), .Carry(full_adder_6_carry));
  Full_Adder full_adder_7 (.Carry_in(full_adder_6_carry), .in_2(a6), .b_in(b6), .out_4(r6), .Carry(full_adder_7_carry));
  Full_Adder full_adder_8 (.Carry_in(full_adder_7_carry), .in_2(a7), .b_in(b7), .out_4(r7), .Carry(Overflow));

  // Notes on the sheet:
  //   Const 0
endmodule

module Two_s_complement (
  input  in_1,
  input  in_2,
  input  in_3,
  input  in_4,
  input  in_5,
  input  in_6,
  input  in_7,
  input  in_8,
  output out_9,
  output out_10,
  output out_11,
  output out_12,
  output out_13,
  output out_14,
  output out_15,
  output out_16,
  output out_17
);

  wire button_1_out, not_1_out, not_2_out, not_3_out, not_4_out, not_5_out, not_6_out, not_7_out, not_8_out,
       not_9_out;

  Button button_1 (.out(button_1_out));
  not not_1 (not_1_out, in_1);
  not not_2 (not_2_out, in_2);
  not not_3 (not_3_out, in_3);
  not not_4 (not_4_out, in_4);
  not not_5 (not_5_out, in_5);
  not not_6 (not_6_out, in_6);
  not not_7 (not_7_out, in_7);
  not not_8 (not_8_out, in_8);
  not not_9 (not_9_out, button_1_out);
  Adder_8_bits adder_8_bits_1 (
    .a0(not_1_out), .a1(not_2_out), .a2(not_3_out), .a3(not_4_out), .a4(not_5_out), .a5(not_6_out),
    .a6(not_7_out), .a7(not_8_out), .b0(not_9_out), .b1(button_1_out), .b2(button_1_out), .b3(button_1_out),
    .b4(button_1_out), .b5(button_1_out), .b6(button_1_out), .b7(button_1_out), .r0(out_9), .r1(out_10),
    .r2(out_11), .r3(out_12), .r4(out_13), .r5(out_14), .r6(out_15), .r7(out_16), .Overflow(out_17));
endmodule

module Subtraction (
  input  a0,
  input  a1,
  input  a2,
  input  a3,
  input  a4,
  input  a5,
  input  a6,
  input  a7,
  input  b0,
  input  b1,
  input  b2,
  input  b3,
  input  b4,
  input  b5,
  input  b6,
  input  b7,
  output r0,
  output r1,
  output r2,
  output r3,
  output r4,
  output r5,
  output r6,
  output r7,
  output Overflow
);

  wire button_1_out, full_adder_1_carry, full_adder_2_carry, full_adder_3_carry, full_adder_4_carry,
       full_adder_5_carry, full_adder_6_carry, full_adder_7_carry, two_s_complement_1_out_9,
       two_s_complement_1_out_10, two_s_complement_1_out_11, two_s_complement_1_out_12,
       two_s_complement_1_out_13, two_s_complement_1_out_14, two_s_complement_1_out_15,
       two_s_complement_1_out_16;

  Two_s_complement two_s_complement_1 (
    .in_1(b0), .in_2(b1), .in_3(b2), .in_4(b3), .in_5(b4), .in_6(b5), .in_7(b6), .in_8(b7),
    .out_9(two_s_complement_1_out_9), .out_10(two_s_complement_1_out_10), .out_11(two_s_complement_1_out_11),
    .out_12(two_s_complement_1_out_12), .out_13(two_s_complement_1_out_13),
    .out_14(two_s_complement_1_out_14), .out_15(two_s_complement_1_out_15), .out_16(two_s_complement_1_out_16));  // open: out_17
  Button button_1 (.out(button_1_out));
  Full_Adder full_adder_1 (
    .Carry_in(button_1_out), .in_2(a0), .b_in(two_s_complement_1_out_9), .out_4(r0),
    .Carry(full_adder_1_carry));
  Full_Adder full_adder_2 (
    .Carry_in(full_adder_1_carry), .in_2(a1), .b_in(two_s_complement_1_out_10), .out_4(r1),
    .Carry(full_adder_2_carry));
  Full_Adder full_adder_3 (
    .Carry_in(full_adder_2_carry), .in_2(a2), .b_in(two_s_complement_1_out_11), .out_4(r2),
    .Carry(full_adder_3_carry));
  Full_Adder full_adder_4 (
    .Carry_in(full_adder_3_carry), .in_2(a3), .b_in(two_s_complement_1_out_12), .out_4(r3),
    .Carry(full_adder_4_carry));
  Full_Adder full_adder_5 (
    .Carry_in(full_adder_4_carry), .in_2(a4), .b_in(two_s_complement_1_out_13), .out_4(r4),
    .Carry(full_adder_5_carry));
  Full_Adder full_adder_6 (
    .Carry_in(full_adder_5_carry), .in_2(a5), .b_in(two_s_complement_1_out_14), .out_4(r5),
    .Carry(full_adder_6_carry));
  Full_Adder full_adder_7 (
    .Carry_in(full_adder_6_carry), .in_2(a6), .b_in(two_s_complement_1_out_15), .out_4(r6),
    .Carry(full_adder_7_carry));
  Full_Adder full_adder_8 (
    .Carry_in(full_adder_7_carry), .in_2(a7), .b_in(two_s_complement_1_out_16), .out_4(r7), .Carry(Overflow));

  // Notes on the sheet:
  //   Const 0
endmodule
